# Fritzing sketch Accessories (saved by Fritzing 0.9.3b)
circuit board: 2.8cm x 1.8cm
perfboards: 1

parts:
  S5 = Pushbutton [package="[THT]"]
  S6 = Pushbutton [package="[THT]"]
  J5 = female pin header, 3 pins [form="♀ (female)"]

nets:
  N1: S5.Pin_1, S5.Pin_2, J5.pin3
  GND: S5.Pin_3, S5.Pin_4, S6.Pin_3, S6.Pin_4, J5.pin1
  N2: S6.Pin_1, S6.Pin_2, J5.pin2
